# Fritzing sketch Flowers (saved by Fritzing 0.9.3b)
breadboards: 1

parts:
  Part1 = Arduino Uno (Rev3) - ICSP
  DS1 = DS18B20 1-Wire Temperature Sensor [part_number=DS18B20]
  R1 = Resistor [tolerance=±5% resistance=4.7k package=THT]
  R2 = Resistor [tolerance=±5% resistance=4.7k package=THT]
  R3 = Resistor [tolerance=±5% resistance=10k package=THT]
  LED1 = LED - 5mm [color="Blue (470nm)" package="5 mm [THT]"]

nets:
  5V: Part1.5V, DS1.VDD, R1.Pin_1, R2.Pin_0
  N1: Part1.D2, DS1.DQ, R1.Pin_0
  N2: Part1.D4, R2.Pin_1
  N3: Part1.D7, R3.Pin_1
  GND: Part1.GND, DS1.GND, LED1.anode
  N4: R3.Pin_0, LED1.cathode

notes:
  Czujniki wilgotności
  ->Zielony - A0 na czujniku wilgotnosci gleby
  ->Żółty - A0 na drugim czujniku wilgotnosci gleby
  ->Czarny - Uziemienie
  ->Czerwony - 5V
  Czujnik poziomu cieczy
  -> Czarny - Uziemienie
  -> Czerwony - 5V
  -> Niebieskie - Analog w czujniku poziomu cieczy
  DHT11
  -> Czarny - uziemienie (pin po prawej)
  -> Czerwony - 5V (pin po lewej)
  -> Cyan - Sygnal do pinu 2 od lewej
  ESP_8266
  -> Brązowy - Rx
  -> Żółty - Tx
  -> Czarny - Uziemienie (GND)
  -> Różowy - 3.3V (VCC)
  -> Pomarańczowy - CH_PD
  -> Szary - Reset (RST) (Powinien byc przez rezystor podciagający, ale nie jest;p)
